# Fritzing sketch schematic (saved by Fritzing 0.9.4)
breadboards: 1

parts:
  M1 = Stepper Motor - Bipolar  # not connected
  Raspberry_Pi_1 = Raspberry Pi 3 [part_number=RPI-3-V1.2]
  C2 = Electrolytic Capacitor [capacitance=47µF voltage=16V package="300 mil [THT, electrolytic]"]
  JACK1 = 2.1mm Barrel Jack with Terminal Block
  Mod1 = KY-024 Linear Hall Magnetic Sensor Module [package="Breakout board"]
  LED1 = LEDs [package=led10mm]
  RY1 = KF-301 Relay [package=THT]
  Pololu_A1 = Pololu A4988 [package=SO16]

nets:
  3V3: Raspberry_Pi_1.3v3, Raspberry_Pi_1.3V3, Mod1.+
  GND: Raspberry_Pi_1.GND, Mod1.G, RY1.ground, Pololu_A1.GND
  N1: Raspberry_Pi_1.GIPO6, RY1.signal
  N2: Raspberry_Pi_1.GIPO26, Mod1.D0
  N3: Raspberry_Pi_1.GIPO20, Pololu_A1.STEP
  N4: Raspberry_Pi_1.GIPO16, Pololu_A1.ENABLE
  N5: Raspberry_Pi_1.5V, RY1.power
  N6: C2.-, JACK1.NEG, LED1.A
  N7: C2.+, JACK1.POS, RY1.C
  N8: LED1.C, RY1.NC
  N9: Pololu_A1.RESET, Pololu_A1.SLEEP

custom parts:
  KY-024 Linear Hall Magnetic Sensor Module: KY-024 Linear Hall Magnetic Sensor Module reacts iin the presence of a magnetic field.
  KF-301 Relay: KF-301 SPDT Relay module using SRD-05VDC-SL-C relay.
